# Fritzing sketch Motorised-Turning-Table (saved by Fritzing 0.9.2b)
breadboards: 1

parts:
  Arduino_Uno_(Rev3) = Arduino Uno (Rev3) - ICSP
  IC1 = ULN2003A [package="DIP16 [THT]"]
  Joystick = Thumb Joystick
  Battery = Lilypad Power Supply
  LCD2 = LCD screen 16x2 IIC [part_number=101290]

nets:
  N1: Arduino_Uno_(Rev3).A0, Joystick.HORZ
  N2: Arduino_Uno_(Rev3).A4/SDA, LCD2.SDA
  N3: Arduino_Uno_(Rev3).A5/SCL, LCD2.SCL
  N4: Arduino_Uno_(Rev3).ICSP_MOSI, Arduino_Uno_(Rev3).D11_PWM/MOSI, IC1.In_4
  N5: Arduino_Uno_(Rev3).D8, IC1.In_1
  N6: Arduino_Uno_(Rev3).D9_PWM, IC1.In_2
  N7: Arduino_Uno_(Rev3).D10_PWM/SS, IC1.In_3
  5V: Arduino_Uno_(Rev3).5V, LCD2.VCC
  GND: Arduino_Uno_(Rev3).GND, Joystick.GND, LCD2.GND
  VIN: Arduino_Uno_(Rev3).VIN, Joystick.VCC
  N8: IC1.0V, Battery.GND
  N9: IC1.COM_-_Common, Battery.+

custom parts:
  LCD screen 16x2 IIC: LCD screen with HD44780 controller enables showing text, symbols, value or anything else that comes from Croduino/Arduino. It is capable of showing 16 symbols in two lines and therefore can be used in many projects that need to send clearly visible and legible output information.. • Color of symbols: White • Backlight: Blue • Dimensions: 80 x 36 x 12 mm • Screen dimensions: 64.5 x 16 mm •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
